// Logisim project 8_bit_computer.circ as structural Verilog: 5 circuits, main circuit main
module main (
  input  MODE,
  input  CLRA,
  input  A0,
  input  A1,
  input  A2,
  input  A3,
  input  CLR_RAM,
  input  D0,
  input  D1,
  input  D2,
  input  D3,
  input  D4,
  input  D5,
  input  D6,
  input  D7,
  input  CLRB,
  input  B0,
  input  CLR_INST,
  input  CLR_OUT,
  input  MI,
  input  RI,
  input  RO,
  input  IO,
  input  II,
  input  AI,
  input  AO,
  input  EO,
  input  SU,
  input  BI,
  input  OI,
  input  CE,
  input  CO,
  input  J,
  input  in_34,
  input  in_35,
  input  in_36,
  input  in_37,
  input  in_38,
  input  in_39,
  input  in_40,
  input  in_41,
  input  TST
);

  wire CLK_out, n7486_1_pin1, n7486_1_pin4, n7486_1_pin9, n7486_1_pin12, n74157_1_pin4, n74157_1_pin7,
       n74157_1_pin9, n74157_1_pin12, n74157_1_pin15, n74157_2_pin4, n74157_2_pin7, n74157_2_pin9,
       n74157_2_pin12, n74157_2_pin15, n74157_3_pin4, n74157_3_pin7, n74157_3_pin9, n74157_3_pin12,
       n74157_3_pin15, n74161_1_pin11, n74161_1_pin12, n74161_1_pin13, n74161_1_pin14, n74245_1_pin1,
       n74245_1_pin11, n74245_1_pin12, n74245_1_pin13, n74245_1_pin14, n74245_1_pin15, n74245_1_pin16,
       n74245_1_pin17, n74245_1_pin18, n74245_2_pin1, n74245_3_pin1, n74245_4_pin1, n74245_4_pin2,
       n74245_5_pin1, n74245_6_pin1, n74245_6_pin2, n74245_6_pin3, n74245_6_pin4, n74245_6_pin5,
       n74245_6_pin6, n74245_6_pin19, n74245_7_pin1, n74245_7_pin2, n74245_7_pin3, n74245_7_pin4,
       n74245_7_pin5, n74245_7_pin6, n74245_7_pin7, n74245_7_pin8, n74245_7_pin9, n74245_7_pin19,
       n74273_1_pin1, n74273_1_pin11, n74283_1_pin1, n74283_1_pin2, n74283_1_pin3, n74283_1_pin4,
       n74283_1_pin5, n74283_1_pin6, n74283_1_pin7, n74283_1_pin10, n74283_1_pin11, n74283_1_pin12,
       n74283_1_pin13, n74283_1_pin14, n74283_1_pin15, n74283_2_pin1, n74283_2_pin2, n74283_2_pin4,
       n74283_2_pin6, n74283_2_pin10, n74283_2_pin11, n74283_2_pin13, n74283_2_pin15, not_1_out, not_2_out,
       not_3_out, not_4_out, not_5_out, not_6_out, not_7_out, not_8_out, not_9_out, not_10_out, not_12_out,
       sn74ls173a_2_q1, sn74ls173a_2_q2, sn74ls173a_2_q3, sn74ls173a_2_q4, sn74ls173a_4_q1, sn74ls173a_4_q2,
       sn74ls173a_4_q3, sn74ls173a_4_q4, sn74ls173a_5_q1, sn74ls173a_5_q2, sn74ls173a_5_q3, sn74ls173a_5_q4,
       sn74ls173a_6_q1, sn74ls173a_6_q2, sn74ls173a_6_q3, sn74ls173a_6_q4, sn74ls173a_7_q1, sn74ls173a_7_q2,
       sn74ls173a_7_q3, sn74ls173a_7_q4, sn74ls173a_9_q1, sn74ls173a_9_q2, sn74ls173a_9_q3, sn74ls173a_9_q4;
  wire [3:0] n74273_1_pin9, n74273_1_pin19;

  Clock CLK (.out(CLK_out));
  _74283 u_74283_1 (
    .pin1(n74283_1_pin1), .pin2(n74283_1_pin2), .pin3(n74283_1_pin3), .pin4(n74283_1_pin4),
    .pin5(n74283_1_pin5), .pin6(n74283_1_pin6), .pin7(n74283_1_pin7), .pin15(n74283_1_pin15),
    .pin14(n74283_1_pin14), .pin13(n74283_1_pin13), .pin12(n74283_1_pin12), .pin11(n74283_1_pin11),
    .pin10(n74283_1_pin10));  // open: pin9
  SN74LS173A sn74ls173a_1 (
    .D1(n74245_1_pin18), .G1(not_1_out), .G2(not_1_out), .D2(n74245_1_pin17), .CLK(CLK_out), .M(1'b0),
    .D3(n74245_1_pin16), .D4(n74245_1_pin15), .N(1'b0), .CLR(CLRA), .Q1(n74283_1_pin12), .Q2(n74283_1_pin14),
    .Q3(n74283_1_pin3), .Q4(n74283_1_pin5));
  SN74LS173A sn74ls173a_2 (
    .D1(n74245_1_pin14), .G1(not_1_out), .G2(not_1_out), .D2(n74245_1_pin13), .CLK(CLK_out), .M(1'b0),
    .D3(n74245_1_pin12), .D4(n74245_1_pin11), .N(1'b0), .CLR(CLRA), .Q1(sn74ls173a_2_q1),
    .Q2(sn74ls173a_2_q2), .Q3(sn74ls173a_2_q3), .Q4(sn74ls173a_2_q4));
  not not_1 (not_1_out, AI);
  not not_2 (not_2_out, AO);
  not not_3 (not_3_out, EO);
  _7486 u_7486_1 (
    .pin1(n7486_1_pin1), .pin2(SU), .pin3(n74283_1_pin11), .pin4(n7486_1_pin4), .pin5(SU),
    .pin6(n74283_1_pin15), .pin13(SU), .pin12(n7486_1_pin12), .pin11(n74283_1_pin6), .pin10(SU),
    .pin9(n7486_1_pin9), .pin8(n74283_1_pin2));
  SN74LS173A sn74ls173a_3 (
    .D1(n74245_1_pin18), .G1(not_4_out), .G2(not_4_out), .D2(n74245_1_pin17), .CLK(CLK_out), .M(1'b0),
    .D3(n74245_1_pin16), .D4(n74245_1_pin15), .N(1'b0), .CLR(CLRB), .Q1(n7486_1_pin1), .Q2(n7486_1_pin4),
    .Q3(n7486_1_pin9), .Q4(n7486_1_pin12));
  SN74LS173A sn74ls173a_4 (
    .D1(n74245_1_pin14), .G1(not_4_out), .G2(not_4_out), .D2(n74245_1_pin13), .CLK(CLK_out), .M(1'b0),
    .D3(n74245_1_pin12), .D4(n74245_1_pin11), .N(1'b0), .CLR(CLRB), .Q1(sn74ls173a_4_q1),
    .Q2(sn74ls173a_4_q2), .Q3(sn74ls173a_4_q3), .Q4(sn74ls173a_4_q4));
  not not_4 (not_4_out, BI);
  not not_5 (not_5_out, B0);
  not not_6 (not_6_out, J);
  not not_7 (not_7_out, CO);
  LED led_1 (.in(n74283_1_pin10));
  LED led_2 (.in(n74283_1_pin13));
  LED led_3 (.in(n74283_1_pin1));
  LED led_4 (.in(n74283_1_pin4));
  LED led_5 (.in(n74283_1_pin12));
  LED led_6 (.in(n74283_1_pin14));
  LED led_7 (.in(n74283_1_pin3));
  LED led_8 (.in(n74283_1_pin5));
  LED led_9 (.in(sn74ls173a_2_q1));
  LED led_10 (.in(sn74ls173a_2_q2));
  LED led_11 (.in(sn74ls173a_2_q3));
  LED led_12 (.in(sn74ls173a_2_q4));
  LED led_13 (.in(n74283_2_pin10));
  LED led_14 (.in(n74283_2_pin13));
  LED led_15 (.in(n74283_2_pin1));
  LED led_16 (.in(n74283_2_pin4));
  _74283 u_74283_2 (
    .pin1(n74283_2_pin1), .pin2(n74283_2_pin2), .pin3(sn74ls173a_2_q3), .pin4(n74283_2_pin4),
    .pin5(sn74ls173a_2_q4), .pin6(n74283_2_pin6), .pin7(SU), .pin15(n74283_2_pin15), .pin14(sn74ls173a_2_q2),
    .pin13(n74283_2_pin13), .pin12(sn74ls173a_2_q1), .pin11(n74283_2_pin11), .pin10(n74283_2_pin10),
    .pin9(n74283_1_pin7));
  LED led_17 (.in(n7486_1_pin1));
  LED led_18 (.in(n7486_1_pin4));
  LED led_19 (.in(n7486_1_pin9));
  LED led_20 (.in(n7486_1_pin12));
  LED led_21 (.in(sn74ls173a_4_q1));
  LED led_22 (.in(sn74ls173a_4_q2));
  LED led_23 (.in(sn74ls173a_4_q3));
  LED led_24 (.in(sn74ls173a_4_q4));
  _74245 u_74245_1 (
    .pin1(n74245_1_pin1), .pin2(n74283_1_pin12), .pin3(n74283_1_pin14), .pin4(n74283_1_pin3),
    .pin5(n74283_1_pin5), .pin6(sn74ls173a_2_q1), .pin7(sn74ls173a_2_q2), .pin8(sn74ls173a_2_q3),
    .pin9(sn74ls173a_2_q4), .pin19(not_2_out), .pin18(n74245_1_pin18), .pin17(n74245_1_pin17),
    .pin16(n74245_1_pin16), .pin15(n74245_1_pin15), .pin14(n74245_1_pin14), .pin13(n74245_1_pin13),
    .pin12(n74245_1_pin12), .pin11(n74245_1_pin11));
  _74245 u_74245_2 (
    .pin1(n74245_2_pin1), .pin2(n74283_1_pin10), .pin3(n74283_1_pin13), .pin4(n74283_1_pin1),
    .pin5(n74283_1_pin4), .pin6(n74283_2_pin10), .pin7(n74283_2_pin13), .pin8(n74283_2_pin1),
    .pin9(n74283_2_pin4), .pin19(not_3_out), .pin18(n74245_1_pin18), .pin17(n74245_1_pin17),
    .pin16(n74245_1_pin16), .pin15(n74245_1_pin15), .pin14(n74245_1_pin14), .pin13(n74245_1_pin13),
    .pin12(n74245_1_pin12), .pin11(n74245_1_pin11));
  _7486 u_7486_2 (
    .pin1(sn74ls173a_4_q1), .pin2(SU), .pin3(n74283_2_pin11), .pin4(sn74ls173a_4_q2), .pin5(SU),
    .pin6(n74283_2_pin15), .pin13(SU), .pin12(sn74ls173a_4_q4), .pin11(n74283_2_pin6), .pin10(SU),
    .pin9(sn74ls173a_4_q3), .pin8(n74283_2_pin2));
  _74245 u_74245_3 (
    .pin1(n74245_3_pin1), .pin2(n7486_1_pin1), .pin3(n7486_1_pin4), .pin4(n7486_1_pin9),
    .pin5(n7486_1_pin12), .pin6(sn74ls173a_4_q1), .pin7(sn74ls173a_4_q2), .pin8(sn74ls173a_4_q3),
    .pin9(sn74ls173a_4_q4), .pin19(not_5_out), .pin18(n74245_1_pin18), .pin17(n74245_1_pin17),
    .pin16(n74245_1_pin16), .pin15(n74245_1_pin15), .pin14(n74245_1_pin14), .pin13(n74245_1_pin13),
    .pin12(n74245_1_pin12), .pin11(n74245_1_pin11));
  _74161 u_74161_1 (
    .pin2(CLK_out), .pin3(n74245_1_pin11), .pin4(n74245_1_pin12), .pin5(n74245_1_pin13),
    .pin6(n74245_1_pin14), .pin7(CE), .pin14(n74161_1_pin14), .pin13(n74161_1_pin13), .pin12(n74161_1_pin12),
    .pin11(n74161_1_pin11), .pin10(CE), .pin9(not_6_out));  // open: pin1, pin15
  LED led_25 (.in(n74161_1_pin11));
  LED led_26 (.in(n74161_1_pin12));
  LED led_27 (.in(n74161_1_pin13));
  LED led_28 (.in(n74161_1_pin14));
  _74245 u_74245_4 (
    .pin1(n74245_4_pin1), .pin2(n74245_4_pin2), .pin3(n74245_4_pin2), .pin4(n74245_4_pin2),
    .pin5(n74245_4_pin2), .pin6(n74161_1_pin11), .pin7(n74161_1_pin12), .pin8(n74161_1_pin13),
    .pin9(n74161_1_pin14), .pin19(not_7_out), .pin18(n74245_1_pin18), .pin17(n74245_1_pin17),
    .pin16(n74245_1_pin16), .pin15(n74245_1_pin15), .pin14(n74245_1_pin14), .pin13(n74245_1_pin13),
    .pin12(n74245_1_pin12), .pin11(n74245_1_pin11));
  not not_8 (not_8_out, TST);
  LED led_29 (.in(n74245_1_pin18));
  _74245 u_74245_5 (
    .pin1(n74245_5_pin1), .pin2(in_34), .pin3(in_35), .pin4(in_36), .pin5(in_37), .pin6(in_38), .pin7(in_39),
    .pin8(in_40), .pin9(in_41), .pin19(not_8_out), .pin18(n74245_1_pin18), .pin17(n74245_1_pin17),
    .pin16(n74245_1_pin16), .pin15(n74245_1_pin15), .pin14(n74245_1_pin14), .pin13(n74245_1_pin13),
    .pin12(n74245_1_pin12), .pin11(n74245_1_pin11));
  LED led_30 (.in(n74245_1_pin15));
  LED led_31 (.in(n74245_1_pin14));
  LED led_32 (.in(n74245_1_pin17));
  LED led_33 (.in(n74245_1_pin16));
  LED led_34 (.in(n74245_1_pin13));
  LED led_35 (.in(n74245_1_pin12));
  LED led_36 (.in(n74245_1_pin11));
  SN74LS173A sn74ls173a_5 (
    .D1(n74245_1_pin14), .G1(not_9_out), .G2(not_9_out), .D2(n74245_1_pin13), .CLK(CLK_out), .M(1'b0),
    .D3(n74245_1_pin12), .D4(n74245_1_pin11), .N(1'b0), .CLR(1'b0), .Q1(sn74ls173a_5_q1),
    .Q2(sn74ls173a_5_q2), .Q3(sn74ls173a_5_q3), .Q4(sn74ls173a_5_q4));
  not not_9 (not_9_out, MI);
  SN74LS173A sn74ls173a_6 (
    .D1(n74245_1_pin18), .G1(1'b0), .G2(1'b0), .D2(n74245_1_pin17), .CLK(CLK_out), .M(1'b0),
    .D3(n74245_1_pin16), .D4(n74245_1_pin15), .N(1'b0), .CLR(1'b0), .Q1(sn74ls173a_6_q1),
    .Q2(sn74ls173a_6_q2), .Q3(sn74ls173a_6_q3), .Q4(sn74ls173a_6_q4));
  SN74LS173A sn74ls173a_7 (
    .D1(n74245_1_pin14), .G1(1'b0), .G2(1'b0), .D2(n74245_1_pin13), .CLK(CLK_out), .M(1'b0),
    .D3(n74245_1_pin12), .D4(n74245_1_pin11), .N(1'b0), .CLR(1'b0), .Q1(sn74ls173a_7_q1),
    .Q2(sn74ls173a_7_q2), .Q3(sn74ls173a_7_q3), .Q4(sn74ls173a_7_q4));
  _74245 u_74245_6 (
    .pin1(n74245_6_pin1), .pin2(n74245_6_pin2), .pin3(n74245_6_pin3), .pin4(n74245_6_pin4),
    .pin5(n74245_6_pin5), .pin6(n74245_6_pin6), .pin7(n74245_6_pin6), .pin8(n74245_6_pin6),
    .pin9(n74245_6_pin6), .pin19(n74245_6_pin19), .pin18(n74245_1_pin11), .pin17(n74245_1_pin12),
    .pin16(n74245_1_pin13), .pin15(n74245_1_pin14), .pin14(n74245_1_pin15), .pin13(n74245_1_pin16),
    .pin12(n74245_1_pin17), .pin11(n74245_1_pin18));
  _74273 u_74273_1 (
    .pin1(n74273_1_pin1), .pin2(n74273_1_pin9[3]), .pin3(n74245_1_pin18), .pin4(n74245_1_pin17),
    .pin5(n74273_1_pin9[2]), .pin6(n74273_1_pin9[1]), .pin7(n74245_1_pin16), .pin8(n74245_1_pin15),
    .pin9(n74273_1_pin9[0]), .pin19(n74273_1_pin19[0]), .pin18(n74245_1_pin11), .pin17(n74245_1_pin12),
    .pin16(n74273_1_pin19[1]), .pin15(n74273_1_pin19[2]), .pin14(n74245_1_pin13), .pin13(n74245_1_pin14),
    .pin12(n74273_1_pin19[3]), .pin11(n74273_1_pin11));
  LED led_37 (.in(MODE));
  LED led_38 (.in(n74157_1_pin4));
  _74245 u_74245_7 (
    .pin1(n74245_7_pin1), .pin2(n74245_7_pin2), .pin3(n74245_7_pin3), .pin4(n74245_7_pin4),
    .pin5(n74245_7_pin5), .pin6(n74245_7_pin6), .pin7(n74245_7_pin7), .pin8(n74245_7_pin8),
    .pin9(n74245_7_pin9), .pin19(n74245_7_pin19), .pin18(n74245_1_pin11), .pin17(n74245_1_pin12),
    .pin16(n74245_1_pin13), .pin15(n74245_1_pin14), .pin14(n74245_1_pin15), .pin13(n74245_1_pin16),
    .pin12(n74245_1_pin17), .pin11(n74245_1_pin18));
  LED led_39 (.in(sn74ls173a_9_q1));
  LED led_40 (.in(sn74ls173a_9_q2));
  LED led_41 (.in(sn74ls173a_9_q3));
  LED led_42 (.in(sn74ls173a_9_q4));
  LED led_43 (.in(n74245_6_pin5));
  LED led_44 (.in(n74245_6_pin4));
  LED led_45 (.in(n74245_6_pin3));
  LED led_46 (.in(n74245_6_pin2));
  LED led_47 (.in(not_10_out));
  not not_10 (not_10_out, MODE);
  _74157 u_74157_1 (
    .pin1(MODE), .pin2(A0), .pin3(sn74ls173a_5_q1), .pin4(n74157_1_pin4), .pin5(A1), .pin6(sn74ls173a_5_q2),
    .pin7(n74157_1_pin7), .pin15(n74157_1_pin15), .pin14(A3), .pin13(sn74ls173a_5_q4),
    .pin12(n74157_1_pin12), .pin11(A2), .pin10(sn74ls173a_5_q3), .pin9(n74157_1_pin9));
  LED led_48 (.in(n74157_1_pin7));
  LED led_49 (.in(n74157_1_pin9));
  LED led_50 (.in(n74157_1_pin12));
  SN74LS189 sn74ls189_1 (
    .WE(RI), .D0(n74157_2_pin4), .D1(n74157_2_pin7), .D2(n74157_2_pin9), .D3(n74157_2_pin12), .CLR(CLR_RAM),
    .A1(n74157_1_pin4), .A2(n74157_1_pin7), .A3(n74157_1_pin9), .A4(n74157_1_pin12), .O1(n74245_7_pin9),
    .O2(n74245_7_pin8), .O3(n74245_7_pin7), .O4(n74245_7_pin6));
  LED led_51 (.in(n74245_7_pin9));
  LED led_52 (.in(n74245_7_pin8));
  LED led_53 (.in(n74245_7_pin7));
  LED led_54 (.in(n74245_7_pin6));
  not not_11 (n74245_7_pin19, RO);
  _74157 u_74157_2 (
    .pin1(MODE), .pin2(D0), .pin3(sn74ls173a_6_q1), .pin4(n74157_2_pin4), .pin5(D1), .pin6(sn74ls173a_6_q2),
    .pin7(n74157_2_pin7), .pin15(n74157_2_pin15), .pin14(D3), .pin13(sn74ls173a_6_q4),
    .pin12(n74157_2_pin12), .pin11(D2), .pin10(sn74ls173a_6_q3), .pin9(n74157_2_pin9));
  _74157 u_74157_3 (
    .pin1(MODE), .pin2(D4), .pin3(sn74ls173a_7_q1), .pin4(n74157_3_pin4), .pin5(D5), .pin6(sn74ls173a_7_q2),
    .pin7(n74157_3_pin7), .pin15(n74157_3_pin15), .pin14(D7), .pin13(sn74ls173a_7_q4),
    .pin12(n74157_3_pin12), .pin11(D6), .pin10(sn74ls173a_7_q3), .pin9(n74157_3_pin9));
  SN74LS173A sn74ls173a_8 (
    .D1(n74245_1_pin14), .G1(not_12_out), .G2(not_12_out), .D2(n74245_1_pin13), .CLK(CLK_out), .M(1'b0),
    .D3(n74245_1_pin12), .D4(n74245_1_pin11), .N(1'b0), .CLR(CLR_INST), .Q1(n74245_6_pin5),
    .Q2(n74245_6_pin4), .Q3(n74245_6_pin3), .Q4(n74245_6_pin2));
  SN74LS173A sn74ls173a_9 (
    .D1(n74245_1_pin18), .G1(not_12_out), .G2(not_12_out), .D2(n74245_1_pin17), .CLK(CLK_out), .M(1'b0),
    .D3(n74245_1_pin16), .D4(n74245_1_pin15), .N(1'b0), .CLR(CLR_INST), .Q1(sn74ls173a_9_q1),
    .Q2(sn74ls173a_9_q2), .Q3(sn74ls173a_9_q3), .Q4(sn74ls173a_9_q4));
  Hex_Digit_Display #(.decimalPoint("false")) hex_digit_display_1 (.value(n74273_1_pin9));
  Hex_Digit_Display #(.decimalPoint("false")) hex_digit_display_2 (.value(n74273_1_pin19));
  and and_1 (n74273_1_pin11, OI, CLK_out);
  LED led_55 (.in(n74157_2_pin4));
  LED led_56 (.in(n74157_2_pin7));
  LED led_57 (.in(n74157_2_pin9));
  SN74LS189 sn74ls189_2 (
    .WE(RI), .D0(n74157_3_pin4), .D1(n74157_3_pin7), .D2(n74157_3_pin9), .D3(n74157_3_pin12), .CLR(CLR_RAM),
    .A1(n74157_1_pin4), .A2(n74157_1_pin7), .A3(n74157_1_pin9), .A4(n74157_1_pin12), .O1(n74245_7_pin5),
    .O2(n74245_7_pin4), .O3(n74245_7_pin3), .O4(n74245_7_pin2));
  LED led_58 (.in(n74245_7_pin5));
  LED led_59 (.in(n74245_7_pin4));
  LED led_60 (.in(n74245_7_pin3));
  LED led_61 (.in(n74245_7_pin2));
  not not_12 (not_12_out, II);
  not not_13 (n74245_6_pin19, IO);
  LED led_62 (.in(n74157_2_pin12));
  LED led_63 (.in(n74157_3_pin4));
  LED led_64 (.in(n74157_3_pin7));
  LED led_65 (.in(n74157_3_pin9));
  not not_14 (n74273_1_pin1, CLR_OUT);
  LED led_66 (.in(n74157_3_pin12));
  LED led_67 (.in(MI));
  LED led_68 (.in(RI));
  LED led_69 (.in(RO));
  LED led_70 (.in(IO));
  LED led_71 (.in(II));
  LED led_72 (.in(AI));
  LED led_73 (.in(AO));
  LED led_74 (.in(EO));
  LED led_75 (.in(SU));
  LED led_76 (.in(BI));
  LED led_77 (.in(OI));
  LED led_78 (.in(CE));
  LED led_79 (.in(CO));
  LED led_80 (.in(J));
  // also tied to GND on the sheet: {n74245_4_pin2, n74245_6_pin6, n74157_1_pin15, n74157_2_pin15, n74157_3_pin15}
  // also tied to VCC on the sheet: {n74245_2_pin1, n74245_1_pin1, n74245_3_pin1, n74245_4_pin1, n74245_5_pin1, n74245_6_pin1, n74245_7_pin1}
endmodule

module SN74LS173A (
  input  M,
  input  N,
  input  D1,
  input  G1,
  input  G2,
  input  D2,
  input  CLK,
  input  D3,
  input  D4,
  input  CLR,
  output Q1,
  output Q2,
  output Q3,
  output Q4
);

  wire and_1_out, and_2_out, and_3_out, and_4_out, and_5_out, and_6_out, and_7_out, and_8_out, and_9_out,
       and_10_out, d_ff_1_q, d_ff_1_qn, d_ff_2_q, d_ff_2_qn, d_ff_3_q, d_ff_3_qn, d_ff_4_q, d_ff_4_qn,
       not_1_out, not_2_out, not_3_out, not_4_out, not_5_out, not_6_out, not_7_out, not_8_out, not_9_out,
       not_10_out, not_11_out, not_12_out, not_13_out, not_14_out, not_15_out, or_1_out, or_2_out, or_3_out,
       or_4_out;

  not not_1 (not_1_out, M);
  not not_2 (not_2_out, N);
  not not_3 (not_3_out, G1);
  not not_4 (not_4_out, G2);
  not not_5 (not_5_out, CLK);
  and and_1 (and_1_out, not_1_out, not_2_out);
  and and_2 (and_2_out, not_3_out, not_4_out);
  not not_6 (not_6_out, and_2_out);
  and and_3 (and_3_out, d_ff_1_q, not_6_out);
  and and_4 (and_4_out, D1, and_2_out);
  and and_5 (and_5_out, d_ff_2_q, not_6_out);
  and and_6 (and_6_out, D2, and_2_out);
  and and_7 (and_7_out, d_ff_3_q, not_6_out);
  and and_8 (and_8_out, D3, and_2_out);
  and and_9 (and_9_out, d_ff_4_q, not_6_out);
  and and_10 (and_10_out, D4, and_2_out);
  not not_7 (not_7_out, CLR);
  or or_1 (or_1_out, and_3_out, and_4_out);
  not not_8 (not_8_out, not_7_out);
  or or_2 (or_2_out, and_5_out, and_6_out);
  not not_9 (not_9_out, not_7_out);
  or or_3 (or_3_out, and_7_out, and_8_out);
  not not_10 (not_10_out, not_7_out);
  or or_4 (or_4_out, and_9_out, and_10_out);
  not not_11 (not_11_out, not_7_out);
  D_Flip_Flop d_ff_1 (.D(or_1_out), .clk(not_5_out), .Q(d_ff_1_q), .Qn(d_ff_1_qn), .reset(not_8_out));  // open: preset
  D_Flip_Flop d_ff_2 (.D(or_2_out), .clk(not_5_out), .Q(d_ff_2_q), .Qn(d_ff_2_qn), .reset(not_9_out));  // open: preset
  D_Flip_Flop d_ff_3 (.D(or_3_out), .clk(not_5_out), .Q(d_ff_3_q), .Qn(d_ff_3_qn), .reset(not_10_out));  // open: preset
  D_Flip_Flop d_ff_4 (.D(or_4_out), .clk(not_5_out), .Q(d_ff_4_q), .Qn(d_ff_4_qn), .reset(not_11_out));  // open: preset
  not not_12 (not_12_out, d_ff_1_qn);
  not not_13 (not_13_out, d_ff_2_qn);
  not not_14 (not_14_out, d_ff_3_qn);
  not not_15 (not_15_out, d_ff_4_qn);
  assign Q1 = and_1_out ? not_12_out : 1'bz;  // Controlled_Buffer controlled_buffer_1
  assign Q2 = and_1_out ? not_13_out : 1'bz;  // Controlled_Buffer controlled_buffer_2
  assign Q3 = and_1_out ? not_14_out : 1'bz;  // Controlled_Buffer controlled_buffer_3
  assign Q4 = and_1_out ? not_15_out : 1'bz;  // Controlled_Buffer controlled_buffer_4
endmodule

module SN74LS189 (
  input  D0,
  input  D1,
  input  D2,
  input  D3,
  input  CLR,
  input  WE,
  input  A1,
  input  A2,
  input  A3,
  input  A4,
  output O1,
  output O2,
  output O3,
  output O4
);

  wire address_decoder_1_en0, address_decoder_1_en1, address_decoder_1_en2, address_decoder_1_en3,
       address_decoder_1_en4, address_decoder_1_en5, address_decoder_1_en6, address_decoder_1_en7,
       address_decoder_1_en8, address_decoder_1_en9, address_decoder_1_en10, address_decoder_1_en11,
       address_decoder_1_en12, address_decoder_1_en13, address_decoder_1_en14, address_decoder_1_en15,
       and_1_out, and_2_out, and_3_out, and_4_out, and_5_out, and_6_out, and_7_out, and_8_out, and_9_out,
       and_10_out, and_11_out, and_12_out, and_13_out, and_14_out, and_15_out, and_16_out;

  and and_1 (and_1_out, WE, address_decoder_1_en0);
  Address_Decoder address_decoder_1 (
    .A3(A1), .A2(A2), .A1(A3), .A0(A4), .EN0(address_decoder_1_en0), .EN1(address_decoder_1_en1),
    .EN2(address_decoder_1_en2), .EN3(address_decoder_1_en3), .EN4(address_decoder_1_en4),
    .EN5(address_decoder_1_en5), .EN6(address_decoder_1_en6), .EN7(address_decoder_1_en7),
    .EN8(address_decoder_1_en8), .EN9(address_decoder_1_en9), .EN10(address_decoder_1_en10),
    .EN11(address_decoder_1_en11), .EN12(address_decoder_1_en12), .EN13(address_decoder_1_en13),
    .EN14(address_decoder_1_en14), .EN15(address_decoder_1_en15));
  RAM_4_Bit_Block ram_4_bit_block_1 (
    .D0(D0), .WE(and_1_out), .D1(D1), .D2(D2), .D3(D3), .RE(address_decoder_1_en0), .CLR(CLR), .Q0(O1),
    .Q2(O2), .Q3(O3), .Q4(O4));
  and and_2 (and_2_out, WE, address_decoder_1_en1);
  RAM_4_Bit_Block ram_4_bit_block_2 (
    .D0(D0), .WE(and_2_out), .D1(D1), .D2(D2), .D3(D3), .RE(address_decoder_1_en1), .CLR(CLR), .Q0(O1),
    .Q2(O2), .Q3(O3), .Q4(O4));
  and and_3 (and_3_out, WE, address_decoder_1_en2);
  RAM_4_Bit_Block ram_4_bit_block_3 (
    .D0(D0), .WE(and_3_out), .D1(D1), .D2(D2), .D3(D3), .RE(address_decoder_1_en2), .CLR(CLR), .Q0(O1),
    .Q2(O2), .Q3(O3), .Q4(O4));
  and and_4 (and_4_out, WE, address_decoder_1_en3);
  RAM_4_Bit_Block ram_4_bit_block_4 (
    .D0(D0), .WE(and_4_out), .D1(D1), .D2(D2), .D3(D3), .RE(address_decoder_1_en3), .CLR(CLR), .Q0(O1),
    .Q2(O2), .Q3(O3), .Q4(O4));
  and and_5 (and_5_out, WE, address_decoder_1_en4);
  RAM_4_Bit_Block ram_4_bit_block_5 (
    .D0(D0), .WE(and_5_out), .D1(D1), .D2(D2), .D3(D3), .RE(address_decoder_1_en4), .CLR(CLR), .Q0(O1),
    .Q2(O2), .Q3(O3), .Q4(O4));
  and and_6 (and_6_out, WE, address_decoder_1_en5);
  RAM_4_Bit_Block ram_4_bit_block_6 (
    .D0(D0), .WE(and_6_out), .D1(D1), .D2(D2), .D3(D3), .RE(address_decoder_1_en5), .CLR(CLR), .Q0(O1),
    .Q2(O2), .Q3(O3), .Q4(O4));
  and and_7 (and_7_out, WE, address_decoder_1_en6);
  RAM_4_Bit_Block ram_4_bit_block_7 (
    .D0(D0), .WE(and_7_out), .D1(D1), .D2(D2), .D3(D3), .RE(address_decoder_1_en6), .CLR(CLR), .Q0(O1),
    .Q2(O2), .Q3(O3), .Q4(O4));
  and and_8 (and_8_out, WE, address_decoder_1_en7);
  RAM_4_Bit_Block ram_4_bit_block_8 (
    .D0(D0), .WE(and_8_out), .D1(D1), .D2(D2), .D3(D3), .RE(address_decoder_1_en7), .CLR(CLR), .Q0(O1),
    .Q2(O2), .Q3(O3), .Q4(O4));
  and and_9 (and_9_out, WE, address_decoder_1_en8);
  RAM_4_Bit_Block ram_4_bit_block_9 (
    .D0(D0), .WE(and_9_out), .D1(D1), .D2(D2), .D3(D3), .RE(address_decoder_1_en8), .CLR(CLR), .Q0(O1),
    .Q2(O2), .Q3(O3), .Q4(O4));
  and and_10 (and_10_out, WE, address_decoder_1_en9);
  RAM_4_Bit_Block ram_4_bit_block_10 (
    .D0(D0), .WE(and_10_out), .D1(D1), .D2(D2), .D3(D3), .RE(address_decoder_1_en9), .CLR(CLR), .Q0(O1),
    .Q2(O2), .Q3(O3), .Q4(O4));
  and and_11 (and_11_out, WE, address_decoder_1_en10);
  RAM_4_Bit_Block ram_4_bit_block_11 (
    .D0(D0), .WE(and_11_out), .D1(D1), .D2(D2), .D3(D3), .RE(address_decoder_1_en10), .CLR(CLR), .Q0(O1),
    .Q2(O2), .Q3(O3), .Q4(O4));
  and and_12 (and_12_out, WE, address_decoder_1_en11);
  RAM_4_Bit_Block ram_4_bit_block_12 (
    .D0(D0), .WE(and_12_out), .D1(D1), .D2(D2), .D3(D3), .RE(address_decoder_1_en11), .CLR(CLR), .Q0(O1),
    .Q2(O2), .Q3(O3), .Q4(O4));
  and and_13 (and_13_out, WE, address_decoder_1_en12);
  RAM_4_Bit_Block ram_4_bit_block_13 (
    .D0(D0), .WE(and_13_out), .D1(D1), .D2(D2), .D3(D3), .RE(address_decoder_1_en12), .CLR(CLR), .Q0(O1),
    .Q2(O2), .Q3(O3), .Q4(O4));
  and and_14 (and_14_out, WE, address_decoder_1_en13);
  RAM_4_Bit_Block ram_4_bit_block_14 (
    .D0(D0), .WE(and_14_out), .D1(D1), .D2(D2), .D3(D3), .RE(address_decoder_1_en13), .CLR(CLR), .Q0(O1),
    .Q2(O2), .Q3(O3), .Q4(O4));
  and and_15 (and_15_out, WE, address_decoder_1_en14);
  RAM_4_Bit_Block ram_4_bit_block_15 (
    .D0(D0), .WE(and_15_out), .D1(D1), .D2(D2), .D3(D3), .RE(address_decoder_1_en14), .CLR(CLR), .Q0(O1),
    .Q2(O2), .Q3(O3), .Q4(O4));
  and and_16 (and_16_out, WE, address_decoder_1_en15);
  RAM_4_Bit_Block ram_4_bit_block_16 (
    .D0(D0), .WE(and_16_out), .D1(D1), .D2(D2), .D3(D3), .RE(address_decoder_1_en15), .CLR(CLR), .Q0(O1),
    .Q2(O2), .Q3(O3), .Q4(O4));
endmodule

module Address_Decoder (
  input  A3,
  input  A2,
  input  A1,
  input  A0,
  output EN0,
  output EN1,
  output EN2,
  output EN3,
  output EN4,
  output EN5,
  output EN6,
  output EN7,
  output EN8,
  output EN9,
  output EN10,
  output EN11,
  output EN12,
  output EN13,
  output EN14,
  output EN15
);

  wire not_1_out, not_2_out, not_3_out, not_4_out;

  not not_1 (not_1_out, A3);
  not not_2 (not_2_out, A2);
  not not_3 (not_3_out, A1);
  not not_4 (not_4_out, A0);
  and and_1 (EN0, not_4_out, not_3_out, not_2_out, not_1_out);
  and and_2 (EN1, A0, not_3_out, not_2_out, not_1_out);
  and and_3 (EN2, not_4_out, A1, not_2_out, not_1_out);
  and and_4 (EN3, A0, A1, not_2_out, not_1_out);
  and and_5 (EN4, not_4_out, not_3_out, A2, not_1_out);
  and and_6 (EN5, A0, not_3_out, A2, not_1_out);
  and and_7 (EN6, not_4_out, A1, A2, not_1_out);
  and and_8 (EN7, A0, A1, A2, not_1_out);
  and and_9 (EN8, not_4_out, not_3_out, not_2_out, A3);
  and and_10 (EN9, A0, not_3_out, not_2_out, A3);
  and and_11 (EN10, not_4_out, A1, not_2_out, A3);
  and and_12 (EN11, A0, A1, not_2_out, A3);
  and and_13 (EN12, not_4_out, not_3_out, A2, A3);
  and and_14 (EN13, A0, not_3_out, A2, A3);
  and and_15 (EN14, not_4_out, A1, A2, A3);
  and and_16 (EN15, A0, A1, A2, A3);
endmodule

module RAM_4_Bit_Block (
  input  RE,
  input  D0,
  input  WE,
  input  D1,
  input  D2,
  input  D3,
  input  CLR,
  output Q0,
  output Q2,
  output Q3,
  output Q4
);

  wire and_1_out, and_2_out, and_3_out, and_4_out, and_5_out, and_6_out, and_7_out, and_8_out, clock_1_out,
       d_ff_1_q, d_ff_1_qn, d_ff_2_q, d_ff_2_qn, d_ff_3_q, d_ff_3_qn, d_ff_4_q, d_ff_4_qn, not_1_out,
       not_2_out, not_3_out, not_4_out, not_5_out, not_6_out, not_7_out, not_8_out, not_9_out, not_10_out,
       not_11_out, or_1_out, or_2_out, or_3_out, or_4_out;

  Clock clock_1 (.out(clock_1_out));
  not not_1 (not_1_out, clock_1_out);
  not not_2 (not_2_out, WE);
  and and_1 (and_1_out, d_ff_1_q, not_2_out);
  and and_2 (and_2_out, D0, WE);
  and and_3 (and_3_out, d_ff_2_q, not_2_out);
  and and_4 (and_4_out, D1, WE);
  and and_5 (and_5_out, d_ff_3_q, not_2_out);
  and and_6 (and_6_out, D2, WE);
  and and_7 (and_7_out, d_ff_4_q, not_2_out);
  and and_8 (and_8_out, D3, WE);
  not not_3 (not_3_out, CLR);
  or or_1 (or_1_out, and_1_out, and_2_out);
  not not_4 (not_4_out, not_3_out);
  or or_2 (or_2_out, and_3_out, and_4_out);
  not not_5 (not_5_out, not_3_out);
  or or_3 (or_3_out, and_5_out, and_6_out);
  not not_6 (not_6_out, not_3_out);
  or or_4 (or_4_out, and_7_out, and_8_out);
  not not_7 (not_7_out, not_3_out);
  D_Flip_Flop d_ff_1 (.D(or_1_out), .clk(not_1_out), .Q(d_ff_1_q), .Qn(d_ff_1_qn), .reset(not_4_out));  // open: preset
  D_Flip_Flop d_ff_2 (.D(or_2_out), .clk(not_1_out), .Q(d_ff_2_q), .Qn(d_ff_2_qn), .reset(not_5_out));  // open: preset
  D_Flip_Flop d_ff_3 (.D(or_3_out), .clk(not_1_out), .Q(d_ff_3_q), .Qn(d_ff_3_qn), .reset(not_6_out));  // open: preset
  D_Flip_Flop d_ff_4 (.D(or_4_out), .clk(not_1_out), .Q(d_ff_4_q), .Qn(d_ff_4_qn), .reset(not_7_out));  // open: preset
  not not_8 (not_8_out, d_ff_1_qn);
  not not_9 (not_9_out, d_ff_2_qn);
  not not_10 (not_10_out, d_ff_3_qn);
  not not_11 (not_11_out, d_ff_4_qn);
  assign Q0 = RE ? not_8_out : 1'bz;  // Controlled_Buffer controlled_buffer_1
  assign Q2 = RE ? not_9_out : 1'bz;  // Controlled_Buffer controlled_buffer_2
  assign Q3 = RE ? not_10_out : 1'bz;  // Controlled_Buffer controlled_buffer_3
  assign Q4 = RE ? not_11_out : 1'bz;  // Controlled_Buffer controlled_buffer_4
endmodule
